# Fritzing sketch Sketch_18650_2PIN_DRV (saved by Fritzing 0.9.5d)

parts:
  ESP32_-_Back1 = ESP32 - CAM
  M1 = DC Motor
  Vertical_Servo = Basic Servo
  Horizontal_Servo = Basic Servo
  6V_Step_UP = Mini-360 DC-DC Buck converter [package=THT]
  3_7V_with_BMS = Parallel 18650 battery
  C1 = Capacitor [package=cap-pth-small2]
  C2 = Capacitor [package=cap-pth-small2]
  470uF = Capacitor Polarized [package=panasonic_e]
  TP4056 = TP4056 [chip_label=TP4056 package="DIP (Dual Inline) [THT]"]
  S1 = Toggle Switch spst [package=THT]
  M2 = DC Motor
  S2 = H-Bridge with L298N
  470uF_2 = Capacitor Polarized [package=panasonic_e]
  M3 = DC Motor
  C3 = Capacitor [package=cap-pth-small2]
  M4 = DC Motor
  C4 = Capacitor [package=cap-pth-small2]

nets:
  N1: ESP32_-_Back1.GPIO2, S2.IN1
  N2: ESP32_-_Back1.GPIO14, S2.IN2
  N3: ESP32_-_Back1.GPIO15, S2.IN3
  N4: ESP32_-_Back1.GPIO13, S2.IN4
  N5: ESP32_-_Back1.GPIO12, Horizontal_Servo.pulse
  GND: ESP32_-_Back1.GND, Vertical_Servo.gnd, Horizontal_Servo.gnd, 6V_Step_UP.OUT-, 470uF.-, S2.GND, 470uF_2.-
  N6: ESP32_-_Back1.5V, 470uF.+
  N7: ESP32_-_Back1.GPIO3_/_RX, Vertical_Servo.pulse
  N8: M1.pin_1, C1.1, S2.M1-02, M4.pin_1, C4.1
  N9: M1.pin_2, C1.2, S2.M1-01, M4.pin_2, C4.2
  VCC: Vertical_Servo.vcc, Horizontal_Servo.vcc, 6V_Step_UP.OUT+, S2.12V, 470uF_2.+
  N10: 6V_Step_UP.IN-, TP4056.pin6
  N11: 6V_Step_UP.IN+, TP4056.pin3
  N12: 3_7V_with_BMS.+, S1.L1
  N13: C2.1, M2.pin_1, S2.M2-02, M3.pin_1, C3.1
  N14: C2.2, M2.pin_2, S2.M2-01, M3.pin_2, C3.2
  N15: TP4056.pin4, S1.COM
  N16: S2.ENA, S2.ENA-5V
  N17: S2.ENB, S2.ENB-5V

custom parts:
  ESP32 - CAM: The ESP32-CAM has a very competitive small-size camera module that can operate independently as a minimum system with a footprint of only 27*40.5*4.5mm and a deep sleep current of up to 6mA.
  Mini-360 DC-DC Buck converter: Mini-360 DC-DC Buck converter. Tiny buck step down voltage converter, input voltage 4.75 to 23V output 1 to 17V adjustable. Available from ebay and the like.
  Parallel 18650 battery: 2x 18650 battery pack (3.7 Volts)
  TP4056: A DIP stand-in part for whatever IC you want. With 6 pins on a 300mil dual inline package (DIP) footprint.
  Toggle Switch spst: Toggle Switch single pole single throw
  H-Bridge with L298N: h-bridge
